# Fritzing sketch fritzing (saved by Fritzing 0.9.3b)
circuit board: 8.46667cm x 5.64444cm
breadboards: 1

parts:
  Part2 = HTU21D Breakout
  BMP280_Breakout1 = BMP280 Breakout Board [part_number=BMP280]
  Part3 = NRF24L01+ Breakout Board
  U2 = NodeMCU V3.0

nets (from the breadboard view):
  N1: Part2.SCL, BMP280_Breakout1.SCL, U2.D1
  N2: Part2.SDA, BMP280_Breakout1.SDA, U2.D2
  GND: Part2.GND, BMP280_Breakout1.GND, Part3.GND, U2.GND#6, U2.GND#13, U2.GND#16, U2.GND#33
  VCC: Part2.3.3V, BMP280_Breakout1.VCC, Part3.VCC, U2.3V3
  N3: Part3.CE, U2.D4
  N4: Part3.CS, U2.D8
  N5: Part3.SCK, U2.D5
  N6: Part3.MOSI, U2.D7
  N7: Part3.MISO, U2.D6

notes:
  keep sensors away of the nodemcu board, since the voltage regulator heats up

custom parts:
  HTU21D Breakout: This is a breadboard friendly breakout board for the Measurement Specialties high-precision, low-power digital humidity sensor.
  BMP280 Breakout Board: This is a breakout board for the Bosch Sensortec BMP280, "an absolute barometric pressure sensor especially designed for mobile applications." The operation range is 300 to 1100 hPa. Supply voltage is 1.2 to 3.6V. Operating temperature range is -40 to +85 °C.
  NodeMCU V3.0: ESP8266 based NodeMCU
